# Fritzing sketch 01_torpedoProject (saved by Fritzing 0.9.3b)
breadboards: 1

parts:
  Part1 = Arduino Micro (Rev3)  # not connected
  S1 = Momentary Switch [package=ksa_sealed_tac_switch]
  S2 = Momentary Switch [package=ksa_sealed_tac_switch]
  S4 = Momentary Switch [package=ksa_sealed_tac_switch]
  S5 = Momentary Switch [package=ksa_sealed_tac_switch]
  S11 = Momentary Switch [package=ksa_sealed_tac_switch]
  LED1 = LED - 5mm [color="Red (633nm)" package="5 mm [THT]"]  # not connected
  LED2 = LED - 5mm [color="Red (633nm)" package="5 mm [THT]"]  # not connected
  LED3 = LED - 5mm [color="Red (633nm)" package="5 mm [THT]"]  # not connected
  LED4 = LED - 5mm [color="Red (633nm)" package="5 mm [THT]"]  # not connected
  LED5 = LED - 5mm [color="Red (633nm)" package="5 mm [THT]"]  # not connected
  LED6 = LED - 5mm [color="Red (633nm)" package="5 mm [THT]"]  # not connected
  LED7 = LED - 5mm [color="Red (633nm)" package="5 mm [THT]"]  # not connected
  LED8 = LED - 5mm [color="Red (633nm)" package="5 mm [THT]"]  # not connected
  S12 = Momentary Switch [package=ksa_sealed_tac_switch]
  S13 = Momentary Switch [package=ksa_sealed_tac_switch]
  S14 = Momentary Switch [package=ksa_sealed_tac_switch]
  S15 = Momentary Switch [package=ksa_sealed_tac_switch]
  LED10 = LED - 5mm [color="Red (633nm)" package="5 mm [THT]"]  # not connected
  LED11 = LED - 5mm [color="Red (633nm)" package="5 mm [THT]"]  # not connected

nets:
  N1: S1.1, S1.3
  N2: S1.2, S1.4
  N3: S2.1, S2.3
  N4: S2.2, S2.4
  N5: S4.1, S4.3
  N6: S4.2, S4.4
  N7: S5.1, S5.3
  N8: S5.2, S5.4
  N9: S11.1, S11.3
  N10: S11.2, S11.4
  N11: S12.1, S12.3
  N12: S12.2, S12.4
  N13: S13.1, S13.3
  N14: S13.2, S13.4
  N15: S14.1, S14.3
  N16: S14.2, S14.4
  N17: S15.1, S15.3
  N18: S15.2, S15.4
